# Fritzing sketch GPS_radio (saved by Fritzing 0.9.10b)
stripboards: 1

parts:
  Mod1 = seeeduino-xiao
  Part1 = NRF24L01+ Breakout Board
  A1 = GY-NEO6MV2

nets:
  N1: Mod1.D0, A1.Rx
  N2: Mod1.D1, A1.Vcc#1
  N3: Mod1.D2, Part1.CS
  N4: Mod1.D3, Part1.CE
  N5: Mod1.D8, Part1.SCK
  N6: Mod1.D9, Part1.MISO
  N7: Mod1.D10, Part1.MOSI
  3V3: Mod1.3V3, Part1.VCC
  GND: Mod1.GND, Part1.GND, A1.Tx
  N8: Mod1.5V, A1.Vcc#0

notes:
  LCD
  pink-SCL / cyan-SDA

custom parts:
  seeeduino-xiao: Seeeduino XIAO processor board.
  GY-NEO6MV2: Description: Module GPS , type GY-NEO6MV2, pour arduino et autres micro-contrôleurs. Caractéristiques De type GY-NEO6MV2 Alimentation 3V-5V Avec Flight Control EEPROM MWC Antenne large céramique, fort signal, 25 x 25 mm Paramètres de configuration sauvegardés en EEPROM Avec batterie de backup de données LED témoin de signal Module miniaturisé 25 x 35 mm Trou de fixation de 3mm Baud rate par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
