# Fritzing sketch 020424 (saved by Fritzing 0.9.10b)
breadboards: 1

parts:
  Part1 = Arduino Uno (Rev3)
  Part2 = LCD1602-I2C
  SD_card_module1 = SD Card Module
  M1 = NEO-6M GPS Module [part_number=GY-GPS6MV2]
  U1 = RFID RC522 SIP - 8 pins [chip_label="RFID RC522" package="SIP (Single Inline) [THT]"]

nets:
  N1: Part1.D10_PWM/SS, U1.NSS
  N2: Part1.A4/SDA, Part2.SDA
  N3: Part1.A5/SCL, Part2.SCL
  N4: Part1.D2, M1.Tx
  N5: Part1.D3_PWM, M1.Rx
  3V3: Part1.3V3, U1.VCC
  GND: Part2.GND, SD_card_module1.GND, M1.GND, U1.GND
  VCC: Part2.VCC, SD_card_module1.+5, M1.Vcc
  N6: SD_card_module1.MOSI, U1.MOSI
  N7: SD_card_module1.SCK, U1.SCK

custom parts:
  LCD1602-I2C: A standard character display, usually with 2x16 characters. Comes in many colors with LCM1602 IIC attached.
  SD Card Module: SD Card Module Slot Socket Reader For Arduino ARM MCU
  NEO-6M GPS Module: GY-GPS6MV2 NEO-6M GPS Module Module based on U-blox NEO-6M GPS engine, incorporating regulator for 3.3-5V DC input, MS621FE-compatible rechargeable battery for backup and EEPROM for storing configuration settings. Links: NEO-6 series product information page NEO-6 Datasheet
  RFID RC522 SIP - 8 pins: A SIP stand-in part for RFID RC522 . With 8 pins on a 300 mil single inline package (SIP) footprint.
